// Logisim project 41. Johnsonovo SR.circ as structural Verilog: 1 circuit, main circuit main
module main (
);

  wire CLR_out, CP_out, s_r_ff_1_q, s_r_ff_1_qn, s_r_ff_2_q, s_r_ff_2_qn, s_r_ff_3_q, s_r_ff_3_qn,
       s_r_ff_4_q, s_r_ff_4_qn;

  Clock #(.highDuration(1), .lowDuration(1)) CP (.out(CP_out));
  Button CLR (.out(CLR_out));
  LED B0 (.in(s_r_ff_1_q));
  S_R_Flip_Flop s_r_ff_1 (
    .S(s_r_ff_4_qn), .clk(CP_out), .R(s_r_ff_4_q), .Q(s_r_ff_1_q), .Qn(s_r_ff_1_qn), .reset(CLR_out));  // open: preset, en
  S_R_Flip_Flop s_r_ff_2 (
    .S(s_r_ff_1_q), .clk(CP_out), .R(s_r_ff_1_qn), .Q(s_r_ff_2_q), .Qn(s_r_ff_2_qn), .reset(CLR_out));  // open: preset, en
  LED B1 (.in(s_r_ff_2_q));
  LED B2 (.in(s_r_ff_3_q));
  S_R_Flip_Flop s_r_ff_3 (
    .S(s_r_ff_2_q), .clk(CP_out), .R(s_r_ff_2_qn), .Q(s_r_ff_3_q), .Qn(s_r_ff_3_qn), .reset(CLR_out));  // open: preset, en
  LED B3 (.in(s_r_ff_4_q));
  S_R_Flip_Flop s_r_ff_4 (
    .S(s_r_ff_3_q), .clk(CP_out), .R(s_r_ff_3_qn), .Q(s_r_ff_4_q), .Qn(s_r_ff_4_qn), .reset(CLR_out));  // open: preset, en
endmodule
