// Logisim project 42. Johnsonovo - D.circ as structural Verilog: 1 circuit, main circuit main
module main (
);

  wire Clear_out, CP_out, d_ff_1_q, d_ff_2_q, d_ff_3_q, d_ff_4_q, d_ff_4_qn;

  Clock #(.highDuration(1), .lowDuration(1)) CP (.out(CP_out));
  Button Clear (.out(Clear_out));
  D_Flip_Flop d_ff_1 (.clk(CP_out), .D(d_ff_4_qn), .Q(d_ff_1_q), .reset(Clear_out));  // open: Qn, preset, en
  LED led_1 (.in(d_ff_1_q));
  D_Flip_Flop d_ff_2 (.clk(CP_out), .D(d_ff_1_q), .Q(d_ff_2_q), .reset(Clear_out));  // open: Qn, preset, en
  LED led_2 (.in(d_ff_2_q));
  D_Flip_Flop d_ff_3 (.clk(CP_out), .D(d_ff_2_q), .Q(d_ff_3_q), .reset(Clear_out));  // open: Qn, preset, en
  LED led_3 (.in(d_ff_3_q));
  D_Flip_Flop d_ff_4 (.clk(CP_out), .D(d_ff_3_q), .Q(d_ff_4_q), .Qn(d_ff_4_qn), .reset(Clear_out));  // open: preset, en
  LED led_4 (.in(d_ff_4_q));

  // Notes on the sheet:
  //   Johnsonovo brojilo
endmodule
