// Logisim project 54.Asinkrono binarno JK.circ as structural Verilog: 1 circuit, main circuit main
module main (
  input  _1
);

  wire CLR_out, CP_out, j_k_ff_1_q, j_k_ff_2_q, j_k_ff_3_q, not_1_out, not_2_out, not_3_out;

  not not_1 (not_1_out, CP_out);
  Clock #(.highDuration(1), .lowDuration(1)) CP (.out(CP_out));
  Button CLR (.out(CLR_out));
  LED B0 (.in(j_k_ff_1_q));
  J_K_Flip_Flop j_k_ff_1 (.J(_1), .clk(not_1_out), .K(_1), .Q(j_k_ff_1_q), .reset(CLR_out));  // open: Qn, preset, en
  not not_2 (not_2_out, j_k_ff_1_q);
  LED B1 (.in(j_k_ff_2_q));
  J_K_Flip_Flop j_k_ff_2 (.J(_1), .clk(not_2_out), .K(_1), .Q(j_k_ff_2_q), .reset(CLR_out));  // open: Qn, preset, en
  not not_3 (not_3_out, j_k_ff_2_q);
  LED B2 (.in(j_k_ff_3_q));
  J_K_Flip_Flop j_k_ff_3 (.J(_1), .clk(not_3_out), .K(_1), .Q(j_k_ff_3_q), .reset(CLR_out));  // open: Qn, preset, en

  // Notes on the sheet:
  //   B0
  //   B1
  //   B2
endmodule
