// Logisim project adders.circ as structural Verilog: 2 circuits, main circuit halfadder
module halfadder (
  input  x,
  input  y,
  output S,
  output C
);

  wire nand_1_out, nand_2_out, nand_3_out;

  nand nand_1 (nand_1_out, x, y);
  nand nand_2 (nand_2_out, x, nand_1_out);
  nand nand_3 (nand_3_out, nand_1_out, y);
  nand nand_4 (S, nand_2_out, nand_3_out);
  nand nand_5 (C, x, x);
endmodule

module fulladder (
  input  in_1,
  input  in_2,
  input  in_3,
  output out_4,
  output out_5
);

  wire and_1_out, halfadder_1_c, xor_1_out;

  xor xor_1 (xor_1_out, in_1, in_2);
  halfadder halfadder_1 (.x(xor_1_out), .y(in_3), .S(out_4), .C(halfadder_1_c));
  and and_1 (and_1_out, in_1, in_2);
  or or_1 (out_5, halfadder_1_c, and_1_out);
endmodule
