// Logisim project 14. registar s paralelnim upisom i ispisom podatka.circ as structural Verilog: 1 circuit, main circuit main
module main (
  input  D0,
  input  D1,
  input  D2,
  input  D3
);

  wire buffer_1_out, button_1_out, clock_1_out, d_ff_1_q, d_ff_2_q, d_ff_3_q, d_ff_4_q, not_1_out;

  Clock #(.highDuration(1), .lowDuration(1)) clock_1 (.out(clock_1_out));
  not not_1 (not_1_out, clock_1_out);
  Button button_1 (.out(button_1_out));
  LED led_1 (.in(d_ff_1_q));
  D_Flip_Flop d_ff_1 (.clk(not_1_out), .D(D0), .Q(d_ff_1_q), .reset(buffer_1_out));  // open: Qn, preset, en
  buf buffer_1 (buffer_1_out, button_1_out);
  LED led_2 (.in(d_ff_2_q));
  D_Flip_Flop d_ff_2 (.clk(not_1_out), .D(D1), .Q(d_ff_2_q), .reset(buffer_1_out));  // open: Qn, preset, en
  D_Flip_Flop d_ff_3 (.clk(not_1_out), .D(D2), .Q(d_ff_3_q), .reset(buffer_1_out));  // open: Qn, preset, en
  LED led_3 (.in(d_ff_3_q));
  LED led_4 (.in(d_ff_4_q));
  D_Flip_Flop d_ff_4 (.clk(not_1_out), .D(D3), .Q(d_ff_4_q), .reset(buffer_1_out));  // open: Qn, preset, en

  // Notes on the sheet:
  //   Cp
  //   CLR
  //   Q0
  //   Q1
  //   Q2
  //   Q3
endmodule
