// Logisim project 35. 54  Asinkrono binarno.circ as structural Verilog: 1 circuit, main circuit main
module main (
  input  _1
);

  wire CLR_out, CP_out, not_1_out, not_2_out, not_3_out, t_ff_1_q, t_ff_2_q, t_ff_3_q;

  Clock #(.highDuration(1), .lowDuration(1)) CP (.out(CP_out));
  Button CLR (.out(CLR_out));
  LED B0 (.in(t_ff_1_q));
  not not_1 (not_1_out, CP_out);
  T_Flip_Flop t_ff_1 (.clk(not_1_out), .T(_1), .Q(t_ff_1_q), .reset(CLR_out));  // open: Qn, preset, en
  not not_2 (not_2_out, t_ff_1_q);
  LED B1 (.in(t_ff_2_q));
  T_Flip_Flop t_ff_2 (.clk(not_2_out), .T(_1), .Q(t_ff_2_q), .reset(CLR_out));  // open: Qn, preset, en
  not not_3 (not_3_out, t_ff_2_q);
  LED B2 (.in(t_ff_3_q));
  T_Flip_Flop t_ff_3 (.clk(not_3_out), .T(_1), .Q(t_ff_3_q), .reset(CLR_out));  // open: Qn, preset, en
endmodule
