// Logisim project 49. brojilo naprijed natrag.circ as structural Verilog: 1 circuit, main circuit main
module main (
  input  Smjer,
  input  _1
);

  wire and_1_out, and_2_out, CP_out, t_ff_1_q, t_ff_2_q, t_ff_3_q, t_ff_4_q, xor_1_out, xor_2_out, xor_3_out;

  Clock #(.highDuration(1), .lowDuration(1)) CP (.out(CP_out));
  T_Flip_Flop t_ff_1 (.clk(CP_out), .T(_1), .Q(t_ff_1_q));  // open: Qn, preset, reset, en
  LED B0 (.in(xor_1_out));
  xor xor_1 (xor_1_out, Smjer, t_ff_1_q);
  LED B1 (.in(xor_2_out));
  xor xor_2 (xor_2_out, Smjer, t_ff_2_q);
  T_Flip_Flop t_ff_2 (.clk(CP_out), .T(xor_1_out), .Q(t_ff_2_q));  // open: Qn, preset, reset, en
  T_Flip_Flop t_ff_3 (.clk(CP_out), .T(and_1_out), .Q(t_ff_3_q));  // open: Qn, preset, reset, en
  and and_1 (and_1_out, xor_2_out, xor_1_out);
  LED B2 (.in(xor_3_out));
  xor xor_3 (xor_3_out, Smjer, t_ff_3_q);
  and and_2 (and_2_out, xor_3_out, and_1_out);
  LED B3 (.in(t_ff_4_q));
  T_Flip_Flop t_ff_4 (.clk(CP_out), .T(and_2_out), .Q(t_ff_4_q));  // open: Qn, preset, reset, en

  // Notes on the sheet:
  //   B0
  //   B1
  //   B2
  //   B3
endmodule
