// Logisim project 24. posmačni registar-ulijevo.circ as structural Verilog: 1 circuit, main circuit main
module main (
  input  Ulaz,
  output Izlaz
);

  wire button_1_out, clock_1_out, d_ff_2_q, d_ff_3_q, d_ff_4_q;

  Clock #(.highDuration(1), .lowDuration(1)) clock_1 (.out(clock_1_out));
  Button button_1 (.out(button_1_out));
  D_Flip_Flop d_ff_1 (.clk(clock_1_out), .D(d_ff_2_q), .Q(Izlaz), .reset(button_1_out));  // open: Qn, preset, en
  LED led_1 (.in(Izlaz));
  LED led_2 (.in(d_ff_2_q));
  D_Flip_Flop d_ff_2 (.clk(clock_1_out), .D(d_ff_3_q), .Q(d_ff_2_q), .reset(button_1_out));  // open: Qn, preset, en
  D_Flip_Flop d_ff_3 (.clk(clock_1_out), .D(d_ff_4_q), .Q(d_ff_3_q), .reset(button_1_out));  // open: Qn, preset, en
  LED led_3 (.in(d_ff_3_q));
  LED led_4 (.in(d_ff_4_q));
  D_Flip_Flop d_ff_4 (.clk(clock_1_out), .D(Ulaz), .Q(d_ff_4_q), .reset(button_1_out));  // open: Qn, preset, en

  // Notes on the sheet:
  //   Cp
  //   CLR
endmodule
