// Logisim project 35. brojilo_sinhrono8bit.circ as structural Verilog: 1 circuit, main circuit main
module main (
);

  wire and_1_out, and_2_out, and_3_out, and_4_out, and_5_out, and_6_out, Clear_out, clock_1_out, CP_out,
       j_k_ff_1_q, j_k_ff_2_q, j_k_ff_3_q, j_k_ff_4_q, j_k_ff_5_q, j_k_ff_6_q, j_k_ff_7_q, j_k_ff_8_q,
       or_1_out;

  Clock #(.highDuration(1), .lowDuration(1)) clock_1 (.out(clock_1_out));
  or or_1 (or_1_out, clock_1_out, CP_out);
  Button CP (.out(CP_out));
  Button Clear (.out(Clear_out));
  J_K_Flip_Flop j_k_ff_1 (
    .J(1'b1), .clk(or_1_out), .K(1'b1), .Q(j_k_ff_1_q), .reset(Clear_out));  // open: Qn, preset, en
  LED led_1 (.in(j_k_ff_1_q));
  and and_1 (and_1_out, j_k_ff_1_q, j_k_ff_2_q);
  J_K_Flip_Flop j_k_ff_2 (
    .J(j_k_ff_1_q), .clk(or_1_out), .K(j_k_ff_1_q), .Q(j_k_ff_2_q), .reset(Clear_out));  // open: Qn, preset, en
  LED led_2 (.in(j_k_ff_2_q));
  and and_2 (and_2_out, and_1_out, j_k_ff_3_q);
  J_K_Flip_Flop j_k_ff_3 (
    .J(and_1_out), .clk(or_1_out), .K(and_1_out), .Q(j_k_ff_3_q), .reset(Clear_out));  // open: Qn, preset, en
  LED led_3 (.in(j_k_ff_3_q));
  and and_3 (and_3_out, and_2_out, j_k_ff_4_q);
  J_K_Flip_Flop j_k_ff_4 (
    .J(and_2_out), .clk(or_1_out), .K(and_2_out), .Q(j_k_ff_4_q), .reset(Clear_out));  // open: Qn, preset, en
  LED led_4 (.in(j_k_ff_4_q));
  and and_4 (and_4_out, and_3_out, j_k_ff_5_q);
  J_K_Flip_Flop j_k_ff_5 (
    .J(and_3_out), .clk(or_1_out), .K(and_3_out), .Q(j_k_ff_5_q), .reset(Clear_out));  // open: Qn, preset, en
  LED led_5 (.in(j_k_ff_5_q));
  and and_5 (and_5_out, and_4_out, j_k_ff_6_q);
  J_K_Flip_Flop j_k_ff_6 (
    .J(and_4_out), .clk(or_1_out), .K(and_4_out), .Q(j_k_ff_6_q), .reset(Clear_out));  // open: Qn, preset, en
  LED led_6 (.in(j_k_ff_6_q));
  and and_6 (and_6_out, and_5_out, j_k_ff_7_q);
  J_K_Flip_Flop j_k_ff_7 (
    .J(and_5_out), .clk(or_1_out), .K(and_5_out), .Q(j_k_ff_7_q), .reset(Clear_out));  // open: Qn, preset, en
  LED led_7 (.in(j_k_ff_7_q));
  J_K_Flip_Flop j_k_ff_8 (
    .J(and_6_out), .clk(or_1_out), .K(and_6_out), .Q(j_k_ff_8_q), .reset(Clear_out));  // open: Qn, preset, en
  LED led_8 (.in(j_k_ff_8_q));

  // Notes on the sheet:
  //   8-bitno sinkrono brojilo
endmodule
