// Logisim project 60._dekadsko brojilo_ispravak.circ as structural Verilog: 1 circuit, main circuit main
module main (
  input  _1
);

  wire and_1_out, CP_out, not_1_out, not_2_out, not_3_out, not_4_out, not_5_out, not_6_out, t_ff_1_q,
       t_ff_2_q, t_ff_3_q, t_ff_4_q;

  Clock CP (.out(CP_out));
  LED B0 (.in(t_ff_1_q));
  not not_1 (not_1_out, CP_out);
  T_Flip_Flop t_ff_1 (.clk(not_1_out), .T(_1), .Q(t_ff_1_q), .reset(and_1_out));  // open: Qn, preset, en
  not not_2 (not_2_out, t_ff_1_q);
  LED B1 (.in(t_ff_2_q));
  T_Flip_Flop t_ff_2 (.clk(not_2_out), .T(_1), .Q(t_ff_2_q), .reset(and_1_out));  // open: Qn, preset, en
  not not_3 (not_3_out, t_ff_2_q);
  not not_4 (not_4_out, not_5_out);
  not not_5 (not_5_out, and_1_out);
  LED B2 (.in(t_ff_3_q));
  T_Flip_Flop t_ff_3 (.clk(not_3_out), .T(_1), .Q(t_ff_3_q), .reset(not_4_out));  // open: Qn, preset, en
  not not_6 (not_6_out, t_ff_3_q);
  LED B3 (.in(t_ff_4_q));
  T_Flip_Flop t_ff_4 (.clk(not_6_out), .T(_1), .Q(t_ff_4_q), .reset(and_1_out));  // open: Qn, preset, en
  and and_1 (and_1_out, t_ff_4_q, t_ff_2_q);
endmodule
