// Logisim project binarno sinkrono paralelno T.circ as structural Verilog: 1 circuit, main circuit main
module main (
  input  _1
);

  wire and_1_out, and_2_out, CLR_out, CP_out, t_ff_1_q, t_ff_2_q, t_ff_3_q, t_ff_4_q;

  Clock #(.highDuration(1), .lowDuration(1)) CP (.out(CP_out));
  Button CLR (.out(CLR_out));
  LED B0 (.in(t_ff_1_q));
  T_Flip_Flop t_ff_1 (.clk(CP_out), .T(_1), .Q(t_ff_1_q), .reset(CLR_out));  // open: Qn, preset, en
  LED B1 (.in(t_ff_2_q));
  T_Flip_Flop t_ff_2 (.clk(CP_out), .T(t_ff_1_q), .Q(t_ff_2_q), .reset(CLR_out));  // open: Qn, preset, en
  and and_1 (and_1_out, t_ff_2_q, t_ff_1_q);
  LED B2 (.in(t_ff_3_q));
  T_Flip_Flop t_ff_3 (.clk(CP_out), .T(and_1_out), .Q(t_ff_3_q), .reset(CLR_out));  // open: Qn, preset, en
  and and_2 (and_2_out, t_ff_3_q, t_ff_2_q, t_ff_1_q);
  LED B3 (.in(t_ff_4_q));
  T_Flip_Flop t_ff_4 (.clk(CP_out), .T(and_2_out), .Q(t_ff_4_q), .reset(CLR_out));  // open: Qn, preset, en

  // Notes on the sheet:
  //   B0
  //   B1
  //   B0*B1
  //   B2
  //   B3
  //   B0*B1*B2
endmodule
