// Logisim project 4bit adder.circ as structural Verilog: 2 circuits, main circuit main
module main (
  input  a3,
  input  a2,
  input  a1,
  input  a0,
  input  b3,
  input  b2,
  input  b1,
  input  b0,
  input  c0,
  output s0,
  output s1,
  output s2,
  output s3,
  output c4
);

  wire zb_1_c_out, zb_2_c_out, zb_3_c_out;

  zb zb_1 (.a(a0), .b(b0), .c_in(c0), .s(s0), .c_out(zb_1_c_out));
  zb zb_2 (.a(a1), .b(b1), .c_in(zb_1_c_out), .s(s1), .c_out(zb_2_c_out));
  zb zb_3 (.a(a2), .b(b2), .c_in(zb_2_c_out), .s(s2), .c_out(zb_3_c_out));
  zb zb_4 (.a(a3), .b(b3), .c_in(zb_3_c_out), .s(s3), .c_out(c4));

  // Notes on the sheet:
  //   +
endmodule

module zb (
  input  a,
  input  b,
  input  c_in,
  output s,
  output c_out
);

  wire and_1_out, and_2_out, xor_1_out;

  xor xor_1 (xor_1_out, a, b);
  xor xor_2 (s, xor_1_out, c_in);
  and and_1 (and_1_out, xor_1_out, c_in);
  and and_2 (and_2_out, a, b);
  or or_1 (c_out, and_1_out, and_2_out);
endmodule
