// Logisim project ALU.circ as structural Verilog: 2 circuits, main circuit main
module main (
  input  [3:0] A,
  input  [3:0] B,
  input  [2:0] C,
  output [3:0] Carry,
  output [3:0] REZ
);

  wire [2:0] undriven, undriven_2, undriven_3, undriven_4;
  wire [3:0] nbcd_2_p1, nbcd_4_p1, nbcd_4_p5, nbcd_4_p9;

  // NBCD nbcd_1: pin names not known
  // NBCD nbcd_2: pin names not known; wires that end beside it: nbcd_2_p1[0], nbcd_2_p1[1], nbcd_2_p1[2], nbcd_2_p1[3]
  _7_Segment_Display u_7_segment_display_1 (
    .g(nbcd_2_p1[0]), .f(nbcd_2_p1[1]), .a(nbcd_2_p1[2]), .b(nbcd_2_p1[3]), .e(undriven[2]), .d(undriven[1]),
    .c(undriven[0]), .dp(1'b0));
  _7_Segment_Display u_7_segment_display_2 (
    .g(nbcd_4_p1[0]), .f(nbcd_4_p1[1]), .a(nbcd_4_p1[2]), .b(nbcd_4_p1[3]), .e(undriven_2[2]),
    .d(undriven_2[1]), .c(undriven_2[0]), .dp(1'b0));
  alu alu_1 (.A(A), .B(B), .OP(C), .Carry(Carry), .REZ(REZ));
  // NBCD nbcd_3: pin names not known
  // NBCD nbcd_4: pin names not known; wires that end beside it: nbcd_4_p1[0], nbcd_4_p1[1], nbcd_4_p1[2], nbcd_4_p1[3], nbcd_4_p5[0], nbcd_4_p5[1], nbcd_4_p5[2], nbcd_4_p5[3], nbcd_4_p9[0], nbcd_4_p9[1], nbcd_4_p9[2], nbcd_4_p9[3]
  _7_Segment_Display u_7_segment_display_3 (
    .g(nbcd_4_p5[0]), .f(nbcd_4_p5[1]), .a(nbcd_4_p5[2]), .b(nbcd_4_p5[3]), .e(undriven_3[2]),
    .d(undriven_3[1]), .c(undriven_3[0]), .dp(1'b0));
  _7_Segment_Display u_7_segment_display_4 (
    .g(nbcd_4_p9[0]), .f(nbcd_4_p9[1]), .a(nbcd_4_p9[2]), .b(nbcd_4_p9[3]), .e(undriven_4[2]),
    .d(undriven_4[1]), .c(undriven_4[0]), .dp(1'b0));

  // Notes on the sheet:
  //   000 +
  //   001 -
  //   010 *
  //   011 /
  //   100 AND
  //   101 OR
  //   110 XOR
  //   111 NOT A
endmodule

module alu (
  input  [3:0] A,
  input  [3:0] B,
  input  [2:0] OP,
  output [3:0] Carry,
  output [3:0] REZ
);

  wire adder_1_cout, subtractor_1_bout;
  wire [3:0] adder_1_out, and_1_out, bit_extender_1_out, bit_extender_2_out, divider_1_out, divider_1_rem,
       multiplier_1_cout, multiplier_1_out, not_1_out, or_1_out, subtractor_1_out, xor_1_out;

  Adder #(.width(4)) adder_1 (.a(A), .b(B), .out(adder_1_out), .cout(adder_1_cout));  // open: cin
  Subtractor #(.width(4)) subtractor_1 (.a(A), .b(B), .out(subtractor_1_out), .bout(subtractor_1_bout));  // open: bin
  Multiplier #(.width(4)) multiplier_1 (.a(A), .b(B), .out(multiplier_1_out), .cout(multiplier_1_cout));  // open: cin
  Divider #(.width(4)) divider_1 (.a(A), .b(B), .out(divider_1_out), .rem(divider_1_rem));  // open: upper
  assign and_1_out = A & B;  // AND_Gate and_1, 4 bits wide
  assign or_1_out = A | B;  // OR_Gate or_1, 4 bits wide
  assign xor_1_out = A ^ B;  // XOR_Gate xor_1, 4 bits wide
  assign not_1_out = ~A;  // NOT_Gate not_1, 4 bits wide
  assign bit_extender_1_out = {{3{1'b0}}, adder_1_cout};  // Bit_Extender bit_extender_1
  assign bit_extender_2_out = {{3{1'b0}}, subtractor_1_bout};  // Bit_Extender bit_extender_2
  Multiplexer #(.select(3), .width(4)) multiplexer_1 (
    .in0(adder_1_out), .in1(subtractor_1_out), .in2(multiplier_1_out), .in3(divider_1_out), .in4(and_1_out),
    .in5(or_1_out), .in6(xor_1_out), .in7(not_1_out), .out(REZ), .sel(OP));  // open: en
  Multiplexer #(.select(3), .width(4)) multiplexer_2 (
    .in0(bit_extender_1_out), .in1(bit_extender_2_out), .in2(multiplier_1_cout), .in3(divider_1_rem),
    .in4(and_1_out), .in5(or_1_out), .in6(xor_1_out), .in7(not_1_out), .out(Carry), .sel(OP));  // open: en
endmodule
