// Logisim project NCBD.circ as structural Verilog: 9 circuits, main circuit main
module main (
  input  A,
  input  B,
  input  C,
  input  D
);

  wire nbcd_1_out_5, nbcd_1_out_6, nbcd_1_out_7, nbcd_1_out_8, nbcd_1_out_9, nbcd_1_out_10, nbcd_1_out_11;

  NBCD nbcd_1 (
    .in_1(A), .in_2(B), .in_3(C), .in_4(D), .out_5(nbcd_1_out_5), .out_6(nbcd_1_out_6), .out_7(nbcd_1_out_7),
    .out_8(nbcd_1_out_8), .out_9(nbcd_1_out_9), .out_10(nbcd_1_out_10), .out_11(nbcd_1_out_11));
  _7_Segment_Display u_7_segment_display_1 (
    .g(nbcd_1_out_5), .f(nbcd_1_out_6), .a(nbcd_1_out_7), .b(nbcd_1_out_8), .e(nbcd_1_out_9),
    .d(nbcd_1_out_10), .c(nbcd_1_out_11), .dp(1'b0));
endmodule

module NBCD (
  input  in_1,
  input  in_2,
  input  in_3,
  input  in_4,
  output out_5,
  output out_6,
  output out_7,
  output out_8,
  output out_9,
  output out_10,
  output out_11
);

  z1 z1 (.d(in_1), .c(in_2), .b(in_3), .a(in_4), .out_5(out_5));
  z2 z2 (.d(in_1), .c(in_2), .b(in_3), .a(in_4), .out_5(out_6));
  z3 z3 (.d(in_1), .c(in_2), .b(in_3), .a(in_4), .out_5(out_7));
  z4 z4 (.d(in_1), .c(in_2), .b(in_3), .a(in_4), .out_5(out_8));
  z5 z5 (.d(in_1), .c(in_2), .b(in_3), .a(in_4), .out_5(out_9));
  z6 z6 (.d(in_1), .c(in_2), .b(in_3), .a(in_4), .out_5(out_10));
  z7 z7 (.d(in_1), .c(in_2), .b(in_3), .a(in_4), .out_5(out_11));
endmodule

module z1 (
  input  d,
  input  c,
  input  b,
  input  a,
  output out_5
);

  wire and_1_out, and_2_out, and_3_out, and_4_out, and_5_out, not_1_out, not_2_out, not_3_out, not_4_out,
       not_5_out;

  not not_1 (not_1_out, b);
  not not_2 (not_2_out, d);
  not not_3 (not_3_out, a);
  not not_4 (not_4_out, c);
  not not_5 (not_5_out, b);
  and and_1 (and_1_out, not_1_out, c);
  and and_2 (and_2_out, c, not_2_out);
  and and_3 (and_3_out, not_3_out, b, not_4_out);
  and and_4 (and_4_out, a, not_5_out);
  and and_5 (and_5_out, a, d);
  or or_1 (out_5, and_1_out, and_2_out, and_3_out, and_4_out, and_5_out);
endmodule

module z2 (
  input  d,
  input  c,
  input  b,
  input  a,
  output out_5
);

  wire and_1_out, and_2_out, and_3_out, and_4_out, and_5_out, not_1_out, not_2_out, not_3_out, not_4_out,
       not_5_out, not_6_out;

  not not_1 (not_1_out, c);
  not not_2 (not_2_out, d);
  not not_3 (not_3_out, d);
  not not_4 (not_4_out, a);
  not not_5 (not_5_out, c);
  not not_6 (not_6_out, b);
  and and_1 (and_1_out, not_1_out, not_2_out);
  and and_2 (and_2_out, b, not_3_out);
  and and_3 (and_3_out, not_4_out, b, not_5_out);
  and and_4 (and_4_out, a, not_6_out);
  and and_5 (and_5_out, a, c);
  or or_1 (out_5, and_1_out, and_2_out, and_3_out, and_4_out, and_5_out);
endmodule

module z3 (
  input  d,
  input  c,
  input  b,
  input  a,
  output out_5
);

  wire and_1_out, and_2_out, and_3_out, and_4_out, and_5_out, and_6_out, not_1_out, not_2_out, not_3_out,
       not_4_out, not_5_out, not_6_out, not_7_out;

  not not_1 (not_1_out, b);
  not not_2 (not_2_out, d);
  not not_3 (not_3_out, a);
  not not_4 (not_4_out, a);
  not not_5 (not_5_out, b);
  not not_6 (not_6_out, c);
  not not_7 (not_7_out, d);
  and and_1 (and_1_out, not_1_out, not_2_out);
  and and_2 (and_2_out, not_3_out, c);
  and and_3 (and_3_out, not_4_out, b, d);
  and and_4 (and_4_out, b, c);
  and and_5 (and_5_out, a, not_5_out, not_6_out);
  and and_6 (and_6_out, a, not_7_out);
  or or_1 (out_5, and_1_out, and_2_out, and_3_out, and_4_out, and_5_out, and_6_out);
endmodule

module z4 (
  input  d,
  input  c,
  input  b,
  input  a,
  output out_5
);

  wire and_1_out, and_2_out, and_3_out, and_4_out, and_5_out, not_1_out, not_2_out, not_3_out, not_4_out;

  not not_1 (not_1_out, b);
  not not_2 (not_2_out, a);
  not not_3 (not_3_out, c);
  not not_4 (not_4_out, d);
  and and_1 (and_1_out, not_2_out, not_1_out);
  and and_2 (and_2_out, not_2_out, not_3_out, not_4_out);
  and and_3 (and_3_out, not_1_out, not_4_out);
  and and_4 (and_4_out, not_2_out, c, d);
  and and_5 (and_5_out, a, not_3_out, d);
  or or_1 (out_5, and_1_out, and_2_out, and_3_out, and_4_out, and_5_out);
endmodule

module z5 (
  input  d,
  input  c,
  input  b,
  input  a,
  output out_5
);

  wire and_1_out, and_2_out, and_3_out, and_4_out, and_5_out, not_1_out, not_2_out;

  not not_1 (not_1_out, b);
  not not_2 (not_2_out, d);
  and and_1 (and_1_out, not_1_out, not_2_out);
  and and_2 (and_2_out, c, not_2_out);
  and and_3 (and_3_out, a, b, d);
  and and_4 (and_4_out, a, not_2_out);
  and and_5 (and_5_out, a, c);
  or or_1 (out_5, and_1_out, and_2_out, and_3_out, and_4_out, and_5_out);
endmodule

module z6 (
  input  d,
  input  c,
  input  b,
  input  a,
  output out_5
);

  wire and_1_out, and_2_out, and_3_out, and_4_out, and_5_out, not_1_out, not_2_out, not_3_out, not_4_out;

  not not_1 (not_1_out, b);
  not not_2 (not_2_out, a);
  not not_3 (not_3_out, c);
  not not_4 (not_4_out, d);
  and and_1 (and_1_out, not_2_out, not_1_out, not_4_out);
  and and_2 (and_2_out, not_1_out, c, d);
  and and_3 (and_3_out, b, not_3_out, d);
  and and_4 (and_4_out, b, c, not_4_out);
  and and_5 (and_5_out, a, not_3_out);
  or or_1 (out_5, and_1_out, and_2_out, and_3_out, and_4_out, and_5_out);
endmodule

module z7 (
  input  d,
  input  c,
  input  b,
  input  a,
  output out_5
);

  wire and_1_out, and_2_out, and_3_out, and_4_out, and_5_out, not_1_out, not_2_out, not_3_out;

  not not_1 (not_1_out, b);
  not not_2 (not_2_out, a);
  not not_3 (not_3_out, c);
  and and_1 (and_1_out, not_2_out, not_3_out);
  and and_2 (and_2_out, not_2_out, d);
  and and_3 (and_3_out, not_3_out, d);
  and and_4 (and_4_out, not_2_out, b);
  and and_5 (and_5_out, a, not_1_out);
  or or_1 (out_5, and_1_out, and_2_out, and_3_out, and_4_out, and_5_out);
endmodule
