// Logisim project pluzbrajalo.circ as structural Verilog: 2 circuits, main circuit main
module main (
  input  in_1,
  input  in_2,
  output out_3,
  output out_4
);

  xor xor_1 (out_3, in_1, in_2);
  and and_1 (out_4, in_1, in_2);
endmodule

module test (
  input  x,
  input  y
);

  wire main_1_out_3, main_1_out_4;

  main main_1 (.in_1(x), .in_2(y), .out_3(main_1_out_3), .out_4(main_1_out_4));
  LED led_1 (.in(main_1_out_3));
  LED led_2 (.in(main_1_out_4));
endmodule
